# Fritzing sketch LAMP FLASHER.423 (saved by Fritzing 0.9.6b)
circuit board: 8.46667cm x 5.64444cm
breadboards: 1

parts:
  R1 = Photocell (LDR) [package=THT]
  R3 = Resistor [tolerance=±5% power=0.25 resistance=10k package=THT]
  D1 = Rectifier Diode [part_number=1N4001 package="300 mil [THT]"]
  R4 = Resistor [tolerance=±10% power=0.25 resistance=470k package=THT]
  R5 = Resistor [tolerance=±5% power=0.25 resistance=10k package=THT]
  Q1 = NPN-Transistor [package="TO92 [THT]"]
  Q2 = NPN-Transistor [package="TO92 [THT]"]
  LED1 = LEDs [package=fkit-led-1206]
  R6 = Resistor [tolerance=±5% power=0.25 resistance=47k package=THT]
  S1 = Square Pushbutton
  R2 = Resistor [tolerance=±5% power=0.25 resistance=100k package=THT]
  C1 = Ceramic Capacitor [capacitance=0.22µF voltage=35V package="200 mil [THT, multilayer]"]
  BAT1 = Battery Holders [package=battery-aaa]

nets:
  N1: R1.pin_0, R3.Pin_0, R5.Pin_0, LED1.A, S1.leg0, R2.Pin_0, R2.Pin_1
  N2: R1.pin_1, Q1.B
  N3: R3.Pin_1, D1.anode, Q1.C
  N4: D1.cathode, Q2.B
  N5: R4.Pin_0, R4.Pin_1, R5.Pin_1, Q1.E, Q2.E, R6.Pin_0, R6.Pin_1, C1.0, C1.1, BAT1.-
  N6: Q2.C, LED1.C
  N7: S1.leg1, BAT1.+
